# Fritzing sketch wisefu_v1 (saved by Fritzing 0.9.3b)
breadboards: 1

parts:
  Composant1 = Arduino Micro (Rev3)
  Composant4 = Adafruit MicroSD card breakout board [part_number="Adafruit #254"]
  Composant5 = Adafruit Bluefruit LE UART Friend [part_number="Adafruit #2479"]

nets:
  N1: Composant1.MOSI, Composant4.DI
  N2: Composant1.D10_PWM/A10, Composant4.CS
  N3: Composant1.SCK, Composant4.CLK
  N4: Composant1.MISO, Composant4.DO
  GND: Composant1.GND, Composant4.GND, Composant5.GND
  5V: Composant1.5V, Composant4.VCC, Composant5.VIN

custom parts:
  Adafruit MicroSD card breakout board: Not just a simple breakout board, this microSD adapter goes the extra mile - designed for ease of use. Onboard 5v->3v regulator provides 150mA for power-hungry cards 3v level shifting means you can use this with ease on either 3v or 5v systems Uses a proper level shifting chip, not resistors: less problems, and faster read/write access Use 3 or 4 digital pins to read and write 2Gb+ of storage!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
  Adafruit Bluefruit LE UART Friend: The Bluefruit LE UART Friend makes it easy to add Bluetooth Low Energy connectivity to anything with a hardware or software serial port. We even have nice hardware flow control so you won't have to think about losing data. Connect to your Arduino or other microcontroller or even just a standard FTDI cable for debugging and testing.
